# Fritzing sketch Keypad-Uno (saved by Fritzing 0.9.3b)
breadboards: 1

parts:
  Part1 = Arduino Uno (Rev3) - ICSP
  S1 = Pushbutton [package="[SMD]"]
  S2 = Pushbutton [package="[SMD]"]
  S3 = Pushbutton [package="[SMD]"]
  S4 = Pushbutton [package="[SMD]"]
  S5 = Pushbutton [package="[SMD]"]
  P2 = Toggle Switch [package=THT]
  J2 = female pin header, 3 pins [form="♀ (female)"]

nets:
  N1: Part1.ICSP_MISO, Part1.D12/MISO, J2.pin2
  N2: Part1.ICSP_MOSI, Part1.D11_PWM/MOSI, J2.pin3
  N3: Part1.D8, S3.Pin_3, S3.Pin_4
  N4: Part1.D9_PWM, S2.Pin_3, S2.Pin_4
  N5: Part1.D10_PWM/SS, S1.Pin_3, S1.Pin_4
  N6: Part1.GND, S1.Pin_1, S1.Pin_2, S2.Pin_1, S2.Pin_2, S3.Pin_1, S3.Pin_2, S4.Pin_1, S4.Pin_2, S5.Pin_1, S5.Pin_2, P2.COM, J2.pin1
  N7: Part1.D5_PWM, P2.L1
  N8: Part1.D6_PWM, S5.Pin_3, S5.Pin_4
  N9: Part1.D7, S4.Pin_3, S4.Pin_4
