# Fritzing sketch Keypad-v2 (saved by Fritzing 0.9.3b)
circuit board: 8cm x 4.4cm
breadboards: 1

parts:
  C = Pushbutton [package="[THT]"]
  D = Pushbutton [package="[THT]"]
  E = Pushbutton [package="[THT]"]
  A = Pushbutton [package="[THT]"]
  B = Pushbutton [package="[THT]"]
  P0 = Toggle Switch [package=THT]
  P1 = Toggle Switch [package=THT]
  C1 = Toggle Switch [package=THT]
  C0 = Toggle Switch [package=THT]
  C2 = Toggle Switch [package=THT]
  C3 = Toggle Switch [package=THT]
  BLE32u4 = Adafruit Feather 32u4 Bluefruit [part_number="Adafruit #2829"]
  J1 = female pin header, 6 pins [form="♀ (female)"]
  23008 = IC, DIP package, 18 pins [chip_label=MCP23008]

nets:
  N1: C.Pin_1, C.Pin_2, BLE32u4.5
  N2: C.Pin_3, C.Pin_4, D.Pin_3, D.Pin_4, E.Pin_3, E.Pin_4, A.Pin_3, A.Pin_4, B.Pin_3, B.Pin_4, P0.COM, P1.COM, C1.COM, C0.COM, C2.COM, C3.COM, BLE32u4.GND, J1.pin1, 23008.pin3, 23008.pin4, 23008.pin5, 23008.pin9
  N3: D.Pin_1, D.Pin_2, BLE32u4.10
  N4: E.Pin_1, E.Pin_2, 23008.pin10
  N5: A.Pin_1, A.Pin_2, BLE32u4.6
  N6: B.Pin_1, B.Pin_2, BLE32u4.9
  N7: P0.L2, 23008.pin11
  N8: P1.L2, 23008.pin12
  N9: C1.L2, 23008.pin14
  N10: C0.L2, 23008.pin13
  N11: C2.L2, 23008.pin15
  N12: C3.L2, 23008.pin16
  N13: BLE32u4.+3V3, 23008.pin6, 23008.pin18
  N14: BLE32u4.12, J1.pin4
  N15: BLE32u4.11, J1.pin5
  N16: BLE32u4.3, 23008.pin1
  N17: BLE32u4.2, 23008.pin2

notes:
  GND
  0/RXD/TXD/0/0
  Parc Keypad v2r1 (C)

custom parts:
  Adafruit Feather 32u4 Bluefruit: This is the Adafruit Feather 32u4 Bluefruit - our take on an 'all-in-one' Arduino-compatible + Bluetooth Low Energy with built in USB and battery charging. Its an Adafruit Feather 32u4 with a BTLE module, ready to rock! We have other boards in the Feather family, check'em out here. Bluetooth Low Energy is the hottest new low-power, 2.4GHz spectrum wireless protocol. In particular, its the only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
